// Digital circuit 4-Bit Adder.dig as structural Verilog
module _4_Bit_Adder (
  input  [3:0] A,
  input  [3:0] B,
  input  _0,
  output OverFlow_flag,
  output [3:0] Sum
);

  wire add_2_c_o, add_3_c_o, add_4_c_o;

  Add add_1 (.a(A[3]), .b(B[3]), .c_i(add_2_c_o), .s(Sum[3]), .c_o(OverFlow_flag));
  Add add_2 (.a(A[2]), .b(B[2]), .c_i(add_3_c_o), .s(Sum[2]), .c_o(add_2_c_o));
  Add add_3 (.a(A[1]), .b(B[1]), .c_i(add_4_c_o), .s(Sum[1]), .c_o(add_3_c_o));
  Add add_4 (.a(A[0]), .b(B[0]), .c_i(_0), .s(Sum[0]), .c_o(add_4_c_o));

  // Notes on the sheet:
  //   A: default 4
  //   B: default 4
endmodule
