// Digital circuit 2-Bit Multiplier.dig as structural Verilog
module _2_Bit_Multiplier (
  input  A0,
  input  B0,
  input  A1,
  input  B0_2,
  input  A0_2,
  input  B1,
  input  B1_2,
  input  A1_2,
  output P0,
  output P1,
  output P2,
  output P3
);

  wire and_2_out, and_3_out, and_4_out, and_5_out;

  and and_1 (P0, A0, B0);
  and and_2 (and_2_out, A1, B0_2);
  and and_3 (and_3_out, A0_2, B1);
  and and_4 (and_4_out, A1_2, B1_2);
  xor xor_1 (P1, and_2_out, and_3_out);
  and and_5 (and_5_out, and_2_out, and_3_out);
  xor xor_2 (P2, and_5_out, and_4_out);
  and and_6 (P3, and_5_out, and_4_out);
endmodule
