// Digital circuit 4-Bit-Register.dig as structural Verilog
module _4_Bit_Register (
  input  Clk,
  input  [3:0] Input,
  input  [1:0] write,
  output [3:0] Output
);

  wire [3:0] multiplexer_1_out, not_1_out;

  Multiplexer #(.Selector_Bits(2), .Bits(4)) multiplexer_1 (
    .sel(write), .in_0(Output), .in_1(Input), .in_2(4'b0000), .in_3(not_1_out), .out(multiplexer_1_out));
  assign not_1_out = ~4'b0000;  // Not not_1, 4 bits wide
  D_FF d_ff_1 (.D(multiplexer_1_out[3]), .C(Clk), .Q(Output[3]));  // open: nQ
  D_FF d_ff_2 (.D(multiplexer_1_out[2]), .C(Clk), .Q(Output[2]));  // open: nQ
  D_FF d_ff_3 (.D(multiplexer_1_out[1]), .C(Clk), .Q(Output[1]));  // open: nQ
  D_FF d_ff_4 (.D(multiplexer_1_out[0]), .C(Clk), .Q(Output[0]));  // open: nQ

  // Notes on the sheet:
  //   Input: default 10
endmodule
