// Digital circuit ALU.dig as structural Verilog
module ALU (
  input  [3:0] A,
  input  [3:0] B,
  input  S_0,
  input  S_1,
  input  C_in,
  output [3:0] D
);

  wire [3:0] multiplexer_1_out, not_1_out;

  assign not_1_out = ~B;  // Not not_1, 4 bits wide
  Multiplexer #(.Selector_Bits(2), .Bits(4)) multiplexer_1 (
    .sel({S_1, S_0}), .in_0(B), .in_1(not_1_out), .in_2(4'b0000), .in_3(4'b1111), .out(multiplexer_1_out));
  _4_Bit_Adder _4_bit_adder_1 (.A(A), .B(multiplexer_1_out), ._0(C_in), .Sum(D));  // open: OverFlow_flag
endmodule
