// Digital circuit Register-File.dig as structural Verilog
module Register_File (
  input  [1:0] Write_Register,
  input  [7:0] Ctrl_Registers,
  input  [3:0] Write_Data,
  input  [1:0] Read_Register1,
  input  [1:0] Read_Register2,
  input  Clk,
  output [3:0] Read_Data1,
  output [3:0] Read_Data2
);

  wire and_1_out, and_2_out, and_3_out, and_4_out, and_5_out, and_6_out, and_7_out, and_8_out,
       Write_Decoder_out_0, Write_Decoder_out_1, Write_Decoder_out_2, Write_Decoder_out_3;
  wire [3:0] R0_p4, R1_p4, R2_p4, R3_p4;

  and and_1 (and_1_out, Ctrl_Registers[0], Ctrl_Registers[1]);
  and and_2 (and_2_out, Ctrl_Registers[2], Ctrl_Registers[3]);
  and and_3 (and_3_out, Ctrl_Registers[4], Ctrl_Registers[5]);
  and and_4 (and_4_out, Ctrl_Registers[6], Ctrl_Registers[7]);
  Decoder #(.Selector_Bits(2), .Bits(2)) Write_Decoder (
    .sel(Write_Register), .out_0(Write_Decoder_out_0), .out_1(Write_Decoder_out_1),
    .out_2(Write_Decoder_out_2), .out_3(Write_Decoder_out_3));
  and and_5 (and_5_out, Write_Decoder_out_0, and_1_out);
  and and_6 (and_6_out, Write_Decoder_out_1, and_2_out);
  and and_7 (and_7_out, Write_Decoder_out_2, and_3_out);
  and and_8 (and_8_out, Write_Decoder_out_3, and_4_out);
  // _4_Bit_Register R0: pin names not known; wires that end beside it: Clk, Write_Data, and_5_out, R0_p4
  // _4_Bit_Register R1: pin names not known; wires that end beside it: Clk, Write_Data, and_6_out, R1_p4
  // _4_Bit_Register R2: pin names not known; wires that end beside it: Clk, Write_Data, and_7_out, R2_p4
  // _4_Bit_Register R3: pin names not known; wires that end beside it: Clk, Write_Data, and_8_out, R3_p4
  Multiplexer #(.Selector_Bits(2), .Bits(4)) Read_Mux1 (
    .sel(Read_Register1), .in_0(R0_p4), .in_1(R1_p4), .in_2(R2_p4), .in_3(R3_p4), .out(Read_Data1));
  Multiplexer #(.Selector_Bits(2), .Bits(4)) Read_Mux2 (
    .sel(Read_Register2), .in_0(R0_p4), .in_1(R1_p4), .in_2(R2_p4), .in_3(R3_p4), .out(Read_Data2));
endmodule
