// Digital circuit 4-Bit-Processor.dig as structural Verilog
module _4_Bit_Processor (
  input  clk,
  input  [1:0] IR_CTRL,
  input  [1:0] Mem_ctrl,
  input  [3:0] Mem_input,
  input  [1:0] pc_ctrl,
  output [3:0] PC_output,
  output [15:0] Instructions_16_bit,
  output [3:0] Read_data_1,
  output [3:0] Read_data_2,
  output [3:0] ALU_out
);

  wire [7:0] registerfile_write_ctrl_1_write_out;

  // intr_mem_module intr_mem_module_1: pin names not known; wires that end beside it: IR_CTRL, pc_ctrl, Mem_ctrl, Mem_input, clk, Instructions_16_bit, PC_output
  RegisterFile_Write_ctrl registerfile_write_ctrl_1 (
    .OpCode3(Instructions_16_bit[1:0]), .write_out(registerfile_write_ctrl_1_write_out));
  Register_File register_file_1 (
    .Sel_read1(Instructions_16_bit[3:2]), .Sel_read2(Instructions_16_bit[5:4]), .clk(clk),
    .Write_data(ALU_out), .Sel_write(Instructions_16_bit[1:0]),
    .CTRL_registers(registerfile_write_ctrl_1_write_out), .Read_data_1(Read_data_1), .Read_data_2(Read_data_2));
  _4_Bit_ALU _4_bit_alu_1 (
    .A(Read_data_1), .B(Read_data_2), .S_1_S_0_C_in(Instructions_16_bit[8:6]), .D(ALU_out));  // open: overflow
endmodule

/* Test case Test-circuit:
IR_CTRL Mem-ctrl Mem-input pc-ctrl clk PC-output Instructions-16-bit ALU-out Read-data_1 Read-data_2
0 1 1 1 c x x x x x
0 1 2 1 c x x x x x
0 1 3 1 c x x x x x
0 1 4 1 c x x x x x
0 1 5 1 c x x x x x
0 1 6 1 c x x x x x
0 1 7 1 c x x x x x
1 0 0 1 c x x x x x
1 0 0 1 c x x x x x
1 0 0 1 c x x x x x
1 0 0 1 c x x x x x
1 0 0 1 c x x x x x
1 0 0 1 c x x x x x
1 0 0 1 c x x x x x
1 0 0 1 c x x x x x
1 0 0 1 c x x x x x
*/
