// Digital circuit 2-bit-updown-counter.dig as structural Verilog
module _2_bit_updown_counter (
  input  clk,
  input  Direction,
  output Q0_plus,
  output Q1_plus
);

  wire Q0_nq, Q1_nq, xnor_1_out, xor_1_out;

  xnor xnor_1 (xnor_1_out, Q0_nq, Q1_nq);
  xor xor_1 (xor_1_out, Direction, xnor_1_out);
  D_FF Q1 (.D(xor_1_out), .C(clk), .Q(Q1_plus), .nQ(Q1_nq));
  D_FF Q0 (.D(Q0_nq), .C(clk), .Q(Q0_plus), .nQ(Q0_nq));
endmodule
