// Digital circuit Hw2-Q7.dig as structural Verilog
module Hw2_Q7 (
  input  I,
  input  clk,
  output S1_plus,
  output S0_plus,
  output X
);

  wire and_1_out, and_2_out, not_1_out, S0_nq;

  and and_1 (and_1_out, S0_nq, not_1_out);
  and and_2 (and_2_out, I, S0_nq, S1_plus);
  D_FF S1 (.D(and_1_out), .C(clk), .nQ(S1_plus));  // open: Q
  D_FF S0 (.D(and_2_out), .C(clk), .Q(S0_plus), .nQ(S0_nq));
  or or_1 (X, not_1_out, S0_nq);
  not not_1 (not_1_out, S1_plus);
endmodule
